# Fritzing sketch qmubeacon_diagram (saved by Fritzing 0.9.3b)
breadboards: 1

parts:
  LoRa32U4 = Adafruit Feather 32u4 RFM9xW LoRa [part_number="Adafruit #3078 and Adafruit #3079"]
  2N7000 = 2N7000 NCH MOSFET [package=to-92]
  1S_LiIon_Battery = DC Power [voltage=5]
  900MHz_Antenna = Antenna

nets:
  N1: LoRa32U4.ANT, 900MHz_Antenna.antenna_lead
  GND: LoRa32U4.GND, 2N7000.S, 1S_LiIon_Battery.V-
  GPS Vcc: LoRa32U4.AREF
  N2: LoRa32U4.VBAT, 1S_LiIon_Battery.V+
  N3: LoRa32U4.12, 2N7000.G
  GPS RX: LoRa32U4.10
  GPS TX: LoRa32U4.9
  GPS GND: 2N7000.D

custom parts:
  Adafruit Feather 32u4 RFM9xW LoRa: This is the Adafruit Feather 32u4 LoRa Radio (RFM9x) - our take on an microcontroller with a "Long Range (LoRa)" packet radio transceiver with built in USB and battery charging. Its an Adafruit Feather 32u4 with a 868/915 MHz radio module cooked in! Great for making wireless networks that can go further than 2.4GHz 802.15.4 and similar, are more flexible than Bluetooth LE and without the high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
  2N7000 NCH MOSFET: 2N7000 NMOS footprint
